// Logisim project SAL-16J-C.circ as structural Verilog
module User_Panel (
  input  [15:0] IN_1,
  input  [15:0] IN_2,
  output CLOCK
);

  wire BKGD, CONT, DONE, ENTER_1, ENTER_2, ERR, HALT, KBD_A, KBD_C, RESET, SCR_C, SCR_E, TTY_C, WAIT_1,
       WAIT_2;
  wire [5:0] FLAGS;
  wire [6:0] KBD_D, TTY_D;
  wire [7:0] SCR_X, SCR_Y;
  wire [15:0] FP, IDX, IR, LR, OUT_1, OUT_2, PC, R0, R1, R2, R3, R4, SCR_D, SP;

  Hex_Digit_Display hex_digit_display_1 (.value(R0[15:12]));  // open: dp
  Hex_Digit_Display hex_digit_display_2 (.value(IDX[15:12]));  // open: dp
  TTY #(.rows(10)) tty_1 (.data(TTY_D), .clk(TTY_C), .we(1'b1), .clr(RESET));
  Keyboard keyboard_1 (.clk(KBD_C), .re(1'b1), .clr(RESET), .avail(KBD_A), .data(KBD_D));
  Hex_Digit_Display hex_digit_display_3 (.value(R0[11:8]));  // open: dp
  Hex_Digit_Display hex_digit_display_4 (.value(R0[7:4]));  // open: dp
  Hex_Digit_Display hex_digit_display_5 (.value(IDX[11:8]));  // open: dp
  Hex_Digit_Display hex_digit_display_6 (.value(IDX[7:4]));  // open: dp
  Hex_Digit_Display hex_digit_display_7 (.value(IN_1[15:12]));  // open: dp
  Hex_Digit_Display hex_digit_display_8 (.value(IN_2[15:12]));  // open: dp
  Hex_Digit_Display hex_digit_display_9 (.value(R0[3:0]));  // open: dp
  Hex_Digit_Display hex_digit_display_10 (.value(IDX[3:0]));  // open: dp
  Hex_Digit_Display hex_digit_display_11 (.value(IN_1[11:8]));  // open: dp
  Hex_Digit_Display hex_digit_display_12 (.value(IN_1[7:4]));  // open: dp
  Hex_Digit_Display hex_digit_display_13 (.value(IN_2[11:8]));  // open: dp
  Hex_Digit_Display hex_digit_display_14 (.value(IN_2[7:4]));  // open: dp
  Hex_Digit_Display hex_digit_display_15 (.value(R1[15:12]));  // open: dp
  Hex_Digit_Display hex_digit_display_16 (.value(R1[11:8]));  // open: dp
  Hex_Digit_Display hex_digit_display_17 (.value(FP[15:12]));  // open: dp
  Hex_Digit_Display hex_digit_display_18 (.value(FP[11:8]));  // open: dp
  LED u_WAIT_1 (.in(WAIT_1));
  Hex_Digit_Display hex_digit_display_19 (.value(IN_1[3:0]));  // open: dp
  LED u_WAIT_2 (.in(WAIT_2));
  Hex_Digit_Display hex_digit_display_20 (.value(IN_2[3:0]));  // open: dp
  Hex_Digit_Display hex_digit_display_21 (.value(R1[7:4]));  // open: dp
  Hex_Digit_Display hex_digit_display_22 (.value(R1[3:0]));  // open: dp
  Hex_Digit_Display hex_digit_display_23 (.value(FP[7:4]));  // open: dp
  Hex_Digit_Display hex_digit_display_24 (.value(FP[3:0]));  // open: dp
  // RGB_Video #(.cursor("No Cursor"), .fixed("ffd7#565 RGB (16 bit)"), .height(256), .scale(1), .width(256)) rgb_video_1: pin names not known; wires that end beside it: RESET, SCR_C, SCR_E, SCR_X, SCR_Y, SCR_D
  Button u_ENTER_1 (.out(ENTER_1));
  Button u_ENTER_2 (.out(ENTER_2));
  Hex_Digit_Display hex_digit_display_25 (.value(R2[15:12]));  // open: dp
  Hex_Digit_Display hex_digit_display_26 (.value(LR[15:12]));  // open: dp
  Hex_Digit_Display hex_digit_display_27 (.value(R2[11:8]));  // open: dp
  Hex_Digit_Display hex_digit_display_28 (.value(R2[7:4]));  // open: dp
  Hex_Digit_Display hex_digit_display_29 (.value(LR[11:8]));  // open: dp
  Hex_Digit_Display hex_digit_display_30 (.value(LR[7:4]));  // open: dp
  Hex_Digit_Display hex_digit_display_31 (.value(OUT_1[15:12]));  // open: dp
  Hex_Digit_Display hex_digit_display_32 (.value(OUT_2[15:12]));  // open: dp
  Hex_Digit_Display hex_digit_display_33 (.value(R2[3:0]));  // open: dp
  Hex_Digit_Display hex_digit_display_34 (.value(LR[3:0]));  // open: dp
  Hex_Digit_Display hex_digit_display_35 (.value(OUT_1[11:8]));  // open: dp
  Hex_Digit_Display hex_digit_display_36 (.value(OUT_1[7:4]));  // open: dp
  Hex_Digit_Display hex_digit_display_37 (.value(OUT_2[11:8]));  // open: dp
  Hex_Digit_Display hex_digit_display_38 (.value(OUT_2[7:4]));  // open: dp
  Hex_Digit_Display hex_digit_display_39 (.value(R3[15:12]));  // open: dp
  Hex_Digit_Display hex_digit_display_40 (.value(R3[11:8]));  // open: dp
  Hex_Digit_Display hex_digit_display_41 (.value(SP[15:12]));  // open: dp
  Hex_Digit_Display hex_digit_display_42 (.value(SP[11:8]));  // open: dp
  Button u_RESET (.out(RESET));
  Hex_Digit_Display hex_digit_display_43 (.value(OUT_1[3:0]));  // open: dp
  Hex_Digit_Display hex_digit_display_44 (.value(OUT_2[3:0]));  // open: dp
  Hex_Digit_Display hex_digit_display_45 (.value(R3[7:4]));  // open: dp
  Hex_Digit_Display hex_digit_display_46 (.value(R3[3:0]));  // open: dp
  Hex_Digit_Display hex_digit_display_47 (.value(SP[7:4]));  // open: dp
  Hex_Digit_Display hex_digit_display_48 (.value(SP[3:0]));  // open: dp
  LED u_DONE (.in(DONE));
  Hex_Digit_Display hex_digit_display_49 (.value(R4[15:12]));  // open: dp
  Hex_Digit_Display hex_digit_display_50 (.value(R4[11:8]));  // open: dp
  Hex_Digit_Display hex_digit_display_51 (.value(PC[15:12]));  // open: dp
  Hex_Digit_Display hex_digit_display_52 (.value(PC[11:8]));  // open: dp
  LED u_ERR (.in(ERR));
  LED C (.in(FLAGS[5]));
  LED A (.in(FLAGS[4]));
  LED E (.in(FLAGS[3]));
  LED Z (.in(FLAGS[2]));
  Hex_Digit_Display hex_digit_display_53 (.value(R4[7:4]));  // open: dp
  Hex_Digit_Display hex_digit_display_54 (.value(R4[3:0]));  // open: dp
  Hex_Digit_Display hex_digit_display_55 (.value(PC[7:4]));  // open: dp
  Hex_Digit_Display hex_digit_display_56 (.value(PC[3:0]));  // open: dp
  LED u_HALT (.in(HALT));
  LED N (.in(FLAGS[1]));
  LED V (.in(FLAGS[0]));
  Hex_Digit_Display hex_digit_display_57 (.value(IR[15:12]));  // open: dp
  Button u_CONT (.out(CONT));
  Logo logo_1 ();
  Hex_Digit_Display hex_digit_display_58 (.value(IR[11:8]));  // open: dp
  Hex_Digit_Display hex_digit_display_59 (.value(IR[7:4]));  // open: dp
  // DipSwitch #(.number(2)) BKGRD: pin names not known; wires that end beside it: BKGD
  Hex_Digit_Display hex_digit_display_60 (.value(IR[3:0]));  // open: dp
  Computer computer_1 (
    .CLOCK(CLOCK), .OUT_1(OUT_1), .SCR_X(SCR_X), .SCR_Y(SCR_Y), .SCR_DATA(SCR_D), .SCR_CLK(SCR_C),
    .SCR_EN(SCR_E), .R0(R0), .R1(R1), .R2(R2), .R3(R3), .R4(R4), .IDX(IDX), .OUT_2(OUT_2), .WAIT_1(WAIT_1),
    .WAIT_2(WAIT_2), .SP(SP), .FLAGS(FLAGS), .PC(PC), .IR(IR), .FP(FP), .LR(LR), .END(DONE),
    .TTY_DATA(TTY_D), .KBD_CLK(KBD_C), .TTY_CLK(TTY_C), .BKGD(BKGD), .KBD_AVAIL(KBD_A), .IN_1(IN_1),
    .IN_2(IN_2), .ENTER_1(ENTER_1), .ENTER_2(ENTER_2), .RESET(RESET), .KBD_DATA(KBD_D), .CONT(CONT),
    .HALT(HALT), .ERR(ERR));  // open: BUS_IN, BUS_OUT

  // Notes on the sheet:
  //   DISPLAY
  //   KEYBOARD
  //   INPUTS
  //   GENERAL PURPOSE REGISTERS
  //   DEDICATED REGISTERS
  //   GRAPHICS SCREEN
  //   OUTPUTS
  //   (or Error Code)
  //   Indicator set if LED is green
  //   ERR set if LED is red
  //   CONTROLS, INDICATORS & FLAGS
  //   NOTES & COMPUTER
  //   REGISTERS
  //   i
  //   g
  //   BKGRD button is set Hi. 
  //   then set up IN_x and press ENTER_x.
  //   NOTES
  //   1. Ensure that MicrocodeLUT.uc is in the control unit's LUT.
  //   2. Ensure that Microcode.uc is in the control unit's ROM.
  //   3. Ensure that TimmiOS.mc is in the computer's ROM.
  //   4. Ensure that the program is in the computer's RAM.
  //   5. If a Graphics Background has been loaded into the
  //   Graphics Unit ROM, and is to be used, ensure that the 
  //   6. Press the RESET button to initilaise the computer.
  //   7. Set 'Auto-Tick Frequency' to 8MHz, then select 'Auto-Tick Enabled'.
  //   8. If any IN_x input is required the WAIT_x led will turn red,
  //   9. The Program has completed when DONE turns green.
  //   10. Press the RESET button to re-run the program.
  //   COMPUTER
endmodule

module Computer (
  input  RESET,
  input  BKGD,
  input  ENTER_1,
  input  ENTER_2,
  input  [6:0] KBD_DATA,
  input  [15:0] IN_1,
  input  [15:0] IN_2,
  input  CONT,
  input  KBD_AVAIL,
  output END,
  output [7:0] SCR_X,
  output [15:0] BUS_IN,
  output [7:0] SCR_Y,
  output [15:0] BUS_OUT,
  output [15:0] SCR_DATA,
  output SCR_CLK,
  output CLOCK,
  output SCR_EN,
  output [15:0] R0,
  output [15:0] R1,
  output [15:0] R2,
  output [15:0] SP,
  output [15:0] R3,
  output [5:0] FLAGS,
  output KBD_CLK,
  output [15:0] R4,
  output [15:0] PC,
  output [15:0] IDX,
  output [15:0] IR,
  output [15:0] FP,
  output HALT,
  output [15:0] LR,
  output [6:0] TTY_DATA,
  output TTY_CLK,
  output [15:0] OUT_1,
  output [15:0] OUT_2,
  output WAIT_1,
  output WAIT_2,
  output ERR
);

  wire address_decoder_1_p3, address_decoder_1_p4, address_decoder_1_p5, and_1_out, and_2_out, and_3_out,
       BG_RDY, cpu_1_ld_gr, cpu_1_mem_e, cpu_1_mem_s, not_1_out, not_2_out, ON_SCR, or_1_out, or_2_out;
  wire [0:0] register_1_q, register_2_q;
  wire [14:0] output_device_3_data, output_device_4_data, output_device_5_data;
  wire [15:0] cpu_1_mem_addr, ram_1_dout, rom_1_data;

  Clock CLK (.out(CLOCK));
  and and_1 (and_1_out, CLOCK, BG_RDY);
  or or_1 (or_1_out, KBD_AVAIL, ENTER_2);
  or or_2 (or_2_out, KBD_AVAIL, ENTER_1);
  CPU cpu_1 (
    .out_8(R0), .out_9(R1), .out_10(R2), .out_28(PC), .out_11(R3), .out_12(R4), .out_29(IR), .out_13(IDX),
    .out_14(FP), .mem_s(cpu_1_mem_s), .mem_e(cpu_1_mem_e), .\end (END), .out_27(SP), .out_15(LR),
    .mem_addr(cpu_1_mem_addr), .bus_out(BUS_OUT), .flags(FLAGS), .bus_in(BUS_IN), .reset(RESET),
    .clkin(and_1_out), .INT_0(or_2_out), .INT_1(or_1_out), .CONT(CONT), .HALT(HALT), .ld_gr(cpu_1_ld_gr),
    .on_scr(ON_SCR));  // open: clk, clks, clke
  // Address_Decoder address_decoder_1: pin names not known; wires that end beside it: cpu_1_mem_addr, cpu_1_ld_gr, address_decoder_1_p3, address_decoder_1_p4, address_decoder_1_p5
  ROM #(.addrWidth(15), .dataWidth(16)) rom_1 (.addr(cpu_1_mem_addr[14:0]), .data(rom_1_data));
  RAM #(.addrWidth(15), .dataWidth(16)) ram_1 (
    .addr(cpu_1_mem_addr[14:0]), .we(address_decoder_1_p4), .clk(cpu_1_mem_s), .din(BUS_OUT),
    .dout(ram_1_dout));
  KBD_Controller kbd_controller_1 (
    .bus_out(BUS_IN), .kbd_clk(KBD_CLK), .id(4'b0001), .addr(cpu_1_mem_addr[3:0]), .data(KBD_DATA),
    .reset(RESET), .clk_e(cpu_1_mem_e), .en(address_decoder_1_p5));
  TTY_Controller tty_controller_1 (
    .data(TTY_DATA), .clk(TTY_CLK), .id(4'b0010), .addr(cpu_1_mem_addr[3:0]), .bus_in(BUS_OUT),
    .clk_s(cpu_1_mem_s), .en(address_decoder_1_p5));
  assign BUS_IN = and_2_out ? rom_1_data : 16'bz;  // Controlled_Buffer controlled_buffer_1
  and and_2 (and_2_out, address_decoder_1_p3, cpu_1_mem_e);
  assign BUS_IN = and_3_out ? ram_1_dout : 16'bz;  // Controlled_Buffer controlled_buffer_2
  and and_3 (and_3_out, address_decoder_1_p4, cpu_1_mem_e);
  Graphics_Unit graphics_unit_1 (
    .bkgd(BKGD), .clk(CLOCK), .bg_rdy(BG_RDY), .en_ld(cpu_1_ld_gr), .on_scr(ON_SCR), .X(SCR_X),
    .set(cpu_1_mem_s), .Y(SCR_Y), .pos(cpu_1_mem_addr), .col(BUS_OUT), .data(SCR_DATA), .reset(RESET),
    .scr_clk(SCR_CLK), .scr_en(SCR_EN));
  Input_Device input_device_1 (
    .bus_out(BUS_IN), .id(4'b0011), .addr(cpu_1_mem_addr[3:0]), .data(IN_1), .reset(RESET),
    .clk_e(cpu_1_mem_e), .en(address_decoder_1_p5));
  Output_Device output_device_1 (
    .data(OUT_1), .id(4'b0110), .addr(cpu_1_mem_addr[3:0]), .bus_in(BUS_OUT), .reset(RESET),
    .clk_s(cpu_1_mem_s), .en(address_decoder_1_p5));
  Input_Device input_device_2 (
    .bus_out(BUS_IN), .id(4'b0111), .addr(cpu_1_mem_addr[3:0]), .data(IN_2), .reset(RESET),
    .clk_e(cpu_1_mem_e), .en(address_decoder_1_p5));
  Output_Device output_device_2 (
    .data(OUT_2), .id(4'b1010), .addr(cpu_1_mem_addr[3:0]), .bus_in(BUS_OUT), .reset(RESET),
    .clk_s(cpu_1_mem_s), .en(address_decoder_1_p5));
  Input_Device input_device_3 (
    .bus_out(BUS_IN), .id(4'b0101), .addr(cpu_1_mem_addr[3:0]), .data({{15{1'b0}}, register_1_q[0]}),
    .reset(RESET), .clk_e(cpu_1_mem_e), .en(address_decoder_1_p5));
  Output_Device output_device_3 (
    .data({output_device_3_data, WAIT_1}), .id(4'b0100), .addr(cpu_1_mem_addr[3:0]), .bus_in(BUS_OUT),
    .reset(RESET), .clk_s(cpu_1_mem_s), .en(address_decoder_1_p5));
  Register #(.width(1)) register_1 (.D(1'b1), .Q(register_1_q[0]), .clk(ENTER_1), .clr(not_1_out));  // open: en
  not not_1 (not_1_out, WAIT_1);
  Input_Device input_device_4 (
    .bus_out(BUS_IN), .id(4'b1001), .addr(cpu_1_mem_addr[3:0]), .data({{15{1'b0}}, register_2_q[0]}),
    .reset(RESET), .clk_e(cpu_1_mem_e), .en(address_decoder_1_p5));
  Output_Device output_device_4 (
    .data({output_device_4_data, WAIT_2}), .id(4'b1000), .addr(cpu_1_mem_addr[3:0]), .bus_in(BUS_OUT),
    .reset(RESET), .clk_s(cpu_1_mem_s), .en(address_decoder_1_p5));
  Register #(.width(1)) register_2 (.D(1'b1), .Q(register_2_q[0]), .clk(ENTER_2), .clr(not_2_out));  // open: en
  not not_2 (not_2_out, WAIT_2);
  Output_Device output_device_5 (
    .data({output_device_5_data, ERR}), .id(4'b0000), .addr(cpu_1_mem_addr[3:0]), .bus_in(BUS_OUT),
    .reset(RESET), .clk_s(cpu_1_mem_s), .en(address_decoder_1_p5));

  // Other names for the same wires on the sheet: CLK = CLOCK

  // Notes on the sheet:
  //   contents of rom_1 (hex, n*v repeats v):
  //   compressed eJy9XUmW5CyvnbMKj78RrY2X43b/S3iIVoCwnVn5v0HVSUdgEELtRRCW88ly95/Q//m/pp3z+IcI
  //   f7Bdxk9u908q5RrGryaxre4/9wkTovlkErJro7o2umtjujYz+kRpa1yrG48vjQTaFXzmSQXqjlVq
  //   dmzaTsd037f71M7HZHepp81Tv7qvNtecuV4m964O70np/jq5o11YPruJCs4W6z47YDzfTsJI/jP3
  //   n4X/jmlZXE+S/5dIiGNu8I4IzW1sZHpifXMRKJUMSAc6eKYDGG4sjH6UgVke2A3xX+xJ+y4CndCS
  //   +e/lDN/PMJKB/zRvSWBeCLRnw7RFStyonjB2nLtjwHXaSWpP1pHJ2uFRh0fmHo9ApbKbY7RJywTN
  //   /GKobdNAeM9ARwX8B5+JxCpPtumITbMEstixu3WVdrPTKedMlmO+gpVMJDjSLkuMqQMD5fJfWKjA
  //   L8XTwH7mp8nLINQKc+CszE0oiXvKS+Go1UyLPNU8joW/6tVgrfQCrxxDIgGabW78ICQSXjzu+3B8
  //   vzJZyxkoOtzinTzzQWxHfFEyxQUogzxzA+EarPskXBt2mit/5hZRgFakrqfDvTxd8a09tEiyuYTH
  //   S8qVOXmHIRY3Xl6NNXTh+5JuHQ43qVMXync1OQMTdHHSoJAvkmFFVDfPpDLNj6wN1o5HAQelCgpn
  //   bV5kCXO03PFcXIsTNnkyBfbNm8YtWMspKgoTjjF6mS6hjfsLOlqPaEvcF2raTpC+wLY70XudoQvP
  //   eq8OSacEDK+mU12FmtkNA0LpSIDe4iJIfsXenCxwWCHf4lG5WM3CKRijj/KovWHYnCq5kYB+L49R
  //   vIJIStcBQ3IpHQOQOEqzT14ML24TU6RZsSzBI8gSPGr/GKQqP06548idnwmNtPSMSXuYxKQTEKeT
  //   jpk6yI8XhFoIGCEEadnWO1K+auaFwMmAF4QpCwKLguDEGgvCdk+gPbDMDPe4L7HHzfivQ4svVtax
  //   JVg8MRcPUtYDaDg3J3va2mjtlNgn53R51eaSvg1/bOP7WR7b3L6f+bmN78c8tVHc96Of2/h+5GMb
  //   4fvhz22gH3XgNkfhvOft6iKWYHtkFjSdhS/LonZLwg6bbNTjX79o5wZY6ZZR2L1Cz5O9tvRgnB/f
  //   LYi6f5DwjZvU5VUDRBasYviLGw7SzNMb7i/fPAzN5Bn+SvIISiNKfONCw0VGKyMTab6ZVz3czqoJ
  //   fFMgcIvDfSFBcZIEEfRodl2vHQl1J7DQ62geLMSLalPEPFJb5y18vJJsIrywAxH4kb3zAdrdLK1Y
  //   meWSdXDm3kRVLHBmqiYojIR7Pc7iiBMLmk5m89rL2fUSYlGbXEnFBHjj2jITYJHdY99BLwz6UN06
  //   u7/DYg1EDXKOQAV7YbEWTtRYErW1ETU/MPOfpQX5hcxp+Qcyp9UPZU7rSubc4yeZ0/oXMtexgF1c
  //   4ldDj3fWWnhgvofAa3mmNgduszI8CjltTPpiKPPCuinaM/ZvqzUoprMMcVm3eKWr9FoRCQ1haaQc
  //   OsN2dqk5WLpUrGVNNe0F9fRCFkN9LLgPPDVMH9ET73qy3/TAG2esCuLFAejzmwPQ195PY4ouWAfG
  //   HFjCPqxWp7etoeyIdZP7QqzhBM9rjWFAPO3NgjKRFEJO8kTiJIz8ptRGSTZ2qE8kKE6SkIyb67q3
  //   K72FHBq3aCGNoeSitGWtcTPuL2Tc4PGLtTfzFQOdJ+MGocyTcYPon3cafGHt2yoNptSCYbLsMZS0
  //   qt26ec7Ocxxm92Oy+OWdjAX+cvLgl//gxBSenX24SPvgSUXLDSDRF1LPg1CKwPt9ZIiedLcmmbQ1
  //   tnE5rMw50LRp0qR1Qr+1wUUb/JjrRljGg7zdydPM7EHeMpcY9b38r81xY5LPU77HE+rl04yc+0KK
  //   q0Nal2hyk50lyIlTSWCFy/MtzNiYLQ25HpMOeV6KPuAl5ZPSbDTiS2Hy+aWF1yPpFVi81C/pGY/E
  //   fCaIXzIzjDSXl5z8GmVr8gx+iYl5hoRBmXokGYBnll7SzUiL126XoOOXMuodX5Ie7EAvnfCSwiMx
  //   fTfk8WYk6/NHWZGnTzSSWyfv2/BL6wIjiWqdUiwQRgoYTf4apaQZ/AmIGU/i8Jyc+nb/nKE6WRVB
  //   nZK6Jy0TlZZBivni3+ZzJ5xL1Q27L9JlYA89X5R9fXAv871h9zLHSODNvSzCS8NVrfMsalnB3yam
  //   TWJbvHcWledZDoLcOuZdxN3nFqxm9N13wxpGL4o33TSpVcuhRV0Mccg9fnILy6L7FSSnWa/gYsZu
  //   p2rnuO1s+Y54HMZ1Ca0HKCoNXKuVmZt1m5uFYtVCVRx+k+PFqlc5Dkr6zIWV4sKDHC+bxHIMj5/k
  //   2IcNilf8kBV76m9f5JjOV630WxD+q323sInBnV1dTjHt1h7geWR4BE8H2SN8PO2rG1Ar2METPGXH
  //   y0mmfmVmLM7slj6uRrR31IYkI1q1lGQgdagDlbCQPgzrxEJVgs2KMpFTD1i5n2OYugd+26mzPPW4
  //   qJZ3FoDMeq1KUeNRZb1dHFWn7jl5JI04e8+Zgz0qURgsQd3NIPVOnGKEkFh9V5wC0GIgJGXbwZpO
  //   C0nxt8tGpMwVpxgdcVacaqwwMUUGUAAlSlNaMZIOVTapXpIzayn/2XbIFMV6lJ7Z9Yf+026V/4TH
  //   L3ZnlZhvQUVn2aQvkJxVhqlOwIhkBjhGaCHmkzMyeYIP8fzqArOwkhnmEcNkBiNB56iVYNTy537Z
  //   gAl4kuMsk4J2Lixgh0zy8Gyv/eJhPoh5iN1W7eQcwGRsblmRv7jBcNbO450eHAQ5xV5djvHFBK7X
  //   SprAod+NXmPV5yfvss4+hZjKBkWBlm/E93W5yHlqagVrAWlxmrT4nQpfnFj8SATSGdaJU4PhvFiY
  //   df1mU9drITQzUVUWYxhCrV9tyL60JiJ8fs7vaoWsdOvNCffG3nS75r/oVXfog2vPwnrVXa0qOvMW
  //   qwlU1dC6q6HV7BVl4B8cDfzb2mxgDmpaCWvdIzvdZgJruXFvX4Q6aVg7kyLOm/o4E2+pXj1V8fkj
  //   aWIlWHqQJpalifAUfsaDOGVkRhr+bS5jWv5ri0ci6tTDTDbVUAkoLal4I6Bcz0w3dAuVZk64cx6l
  //   AnF+dBAD15VvJ9SSKxOqKowN6qsWVoS3oFxLrsJLpSsslag5PnOxu1WtHv1AgrP0sXUfyyUsp/tr
  //   A2pt2PmHmJK5zw6o6wgVUu5JlCzHfwdymthhMdgieQIM3VAsUqBj+UaQ5j2Uv1xA8eLL/OB1jZE7
  //   KElCm4iSmzss6xb6cRyVAGN6Ei4exMM18wlwpizDQDIy+M8RoCxuXWpAe1U0o5Xa0exyetfugill
  //   s+GLRrMlH4YIFcQu+da58C7x6/Wmwlok3ymQA+d1dRgs+XH4MJiVxw9hhOTnRtgLHhbYBTs9/lA8
  //   TaR8pTKTytQfnam/xqY+LtriaLvXLwZSCsjNcKhHD/SWTOUdY1bHCcRqMXLO1JYzHXpga8tba4vC
  //   rroP2qjXsYsUqk3RGc00fVZ0NdsBae1x5cAwSqn3baQw4xAW64lYdoI1X3dbql3sO4HAxSWyKBsb
  //   NcYk2liTLCK4yj605Dmgb9wmZ5lhM7V9UvwaW+rtE+/SiLLBUB8t7ebkeYWCaNiSiDzbj2DcwdyD
  //   YOLvDpW+m9S+2VDBS3dzlG6g6aSVI3kDUsJ/9Zt2X127w7XzX5wm1ZZKcYrksuuSUD8/OygT94XW
  //   NGF3JsyZYFbND+pY8fw8MXQ3zv7VrHie36XgKMCRWIbmJ0U7P7+6DM2vn1rouSNfHSPy0xI4wqCj
  //   8F8m8RLzyfIbjjqbqdO6434JDkb1qIn7LixZoSI0l7lLOZ8N92Uhf9H5u0SbZV0PS5mklpHnrPD8
  //   ONbwZhj78iM66QrMwIy3IuyiLcOq41Jn+iMRgypYT6KpZGOoK3KfvTtM7Z20nO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
endmodule

module CPU (
  input  [15:0] bus_in,
  input  reset,
  input  clkin,
  input  CONT,
  input  INT_0,
  input  INT_1,
  output [15:0] bus_out,
  output [15:0] out_8,
  output [15:0] out_9,
  output [15:0] out_10,
  output [15:0] out_11,
  output [15:0] out_12,
  output [15:0] out_13,
  output [15:0] out_14,
  output [15:0] out_15,
  output [15:0] mem_addr,
  output clk,
  output clks,
  output clke,
  output mem_s,
  output mem_e,
  output \end ,
  output HALT,
  output ld_gr,
  output [5:0] flags,
  output on_scr,
  output [15:0] out_27,
  output [15:0] out_28,
  output [15:0] out_29
);

  wire ACC_p2, ACC_p5, alu_1_p3, alu_1_p4, alu_1_p5, alu_1_p15, and_1_out, and_2_out, and_3_out, and_4_out,
       and_5_out, ASR, CL_EN, clock_1_p6, control_1_ack_int, control_1_fp_e, control_1_ints, control_1_lr_e,
       control_1_lr_s, control_1_mar_s, control_1_on_scr_s, control_1_sp_e, control_1_sp_id, control_1_sp_s,
       d_ff_3_q, FCMP, FLAGS_p2, fpu_1_p3, fpu_1_p8, IDX_p3, IDX_p5, IR_p2, not_1_out, not_2_out, not_3_out,
       not_4_out, not_5_out, ON_SCR_t, or_3_out, or_4_out, program_counter_1_p2, program_counter_1_p3,
       program_counter_1_p7, program_counter_1_p8, R0_p2, R0_p6, R0_p8, R1_p3, R1_p5, R2_p3, R2_p5, R3_p3,
       R3_p5, R4_p3, R4_p5, register_1_p4, set_to_one_1_p1, set_to_one_1_p2, set_to_one_1_p3, TMP_p2;
  wire [1:0] control_1_math_e, d_ff_1_q;
  wire [2:2] maths_unit_1_p1;
  wire [5:0] alu_1_p14, FLAGS_p5, maths_unit_1_p2, multiplexer_1_out;
  wire [15:0] alu_1_p8, fpscrpos_1_p3, fpu_1_p7, IR_p5, maths_unit_1_p6, multiplexer_2_out, multiplexer_3_out;
  wire [31:0] counter_1_q, counter_2_q;

  // Set_To_One set_to_one_1: pin names not known; wires that end beside it: set_to_one_1_p1, set_to_one_1_p2, set_to_one_1_p3
  // Register TMP: pin names not known; wires that end beside it: bus_in, TMP_p2, reset, set_to_one_1_p1, 1'b1, bus_in, set_to_one_1_p1
  // ALU alu_1: pin names not known; wires that end beside it: bus_in, set_to_one_1_p2, alu_1_p3, alu_1_p4, alu_1_p5, ASR, FCMP, alu_1_p8, alu_1_p14[5], alu_1_p14[4], alu_1_p14[3], alu_1_p14[2], alu_1_p14[1], alu_1_p14[0], alu_1_p15
  // FPScrPos fpscrpos_1: pin names not known; wires that end beside it: set_to_one_1_p1, bus_in, fpscrpos_1_p3, ON_SCR_t
  // Maths_Unit maths_unit_1: pin names not known; wires that end beside it: {maths_unit_1_p1[2], out_29[1:0]}, maths_unit_1_p2[0], maths_unit_1_p2[1], maths_unit_1_p2[2], maths_unit_1_p2[5], maths_unit_1_p6
  // FPU fpu_1: pin names not known; wires that end beside it: bus_in, set_to_one_1_p1, fpu_1_p3, clkin, control_1_math_e[1], {maths_unit_1_p1[2], out_29[1:0]}, fpu_1_p7, fpu_1_p8
  or or_1 (fpu_1_p3, reset, IR_p2);
  not not_1 (not_1_out, fpu_1_p8);
  Multiplexer #(.enable("false"), .width(6)) multiplexer_1 (
    .in0(alu_1_p14), .in1({maths_unit_1_p2[5], alu_1_p14[4:3], maths_unit_1_p2[2:0]}),
    .out(multiplexer_1_out), .sel(control_1_math_e[0]));
  and and_1 (and_1_out, not_1_out, control_1_math_e[1]);
  not not_2 (not_2_out, \end );
  and and_2 (and_2_out, not_2_out, CL_EN, fpu_1_p8, clkin);
  and and_3 (and_3_out, INT_0, control_1_ints);
  and and_4 (and_4_out, INT_1, control_1_ints);
  // Clock clock_1: pin names not known; wires that end beside it: reset, and_2_out, clkin, clk, clks, clock_1_p6
  D_Flip_Flop d_ff_1 (.clk(and_3_out), .D(1'b1), .Q(d_ff_1_q[0]), .reset(control_1_ack_int));  // open: Qn, preset
  D_Flip_Flop d_ff_2 (.clk(and_4_out), .D(1'b1), .Q(d_ff_1_q[1]), .reset(control_1_ack_int));  // open: Qn, preset
  or or_2 (clke, clock_1_p6, and_1_out);
  // Register FLAGS: pin names not known; wires that end beside it: multiplexer_1_out, FLAGS_p2, reset, flags, FLAGS_p5, 1'b1
  Multiplexer #(.enable("false"), .select(2), .width(16)) multiplexer_2 (
    .in0(alu_1_p8), .in1(maths_unit_1_p6), .in2(fpu_1_p7), .in3(fpscrpos_1_p3), .out(multiplexer_2_out),
    .sel(control_1_math_e));
  // Register R0: pin names not known; wires that end beside it: bus_in, R0_p2, reset, out_8, bus_in, R0_p6, bus_in, R0_p8, reset
  or or_3 (or_3_out, d_ff_1_q[0], d_ff_1_q[1]);
  // Register R1: pin names not known; wires that end beside it: out_9, bus_in, R1_p3, bus_in, R1_p5, reset
  // Register ACC: pin names not known; wires that end beside it: multiplexer_2_out, ACC_p2, reset, bus_in, ACC_p5
  Multiplexer #(.enable("false"), .select(2), .width(16)) multiplexer_3 (
    .in0(bus_in), .in1(16'h10), .in2(16'h12), .in3(16'h14), .out(multiplexer_3_out), .sel(d_ff_1_q));
  // Register R2: pin names not known; wires that end beside it: out_10, bus_in, R2_p3, bus_in, R2_p5, reset
  // Program_Counter program_counter_1: pin names not known; wires that end beside it: multiplexer_3_out, program_counter_1_p2, program_counter_1_p3, reset, out_28, bus_in, program_counter_1_p7, program_counter_1_p8
  // Register R3: pin names not known; wires that end beside it: out_11, bus_in, R3_p3, bus_in, R3_p5, reset
  // Register R4: pin names not known; wires that end beside it: out_12, bus_in, R4_p3, bus_in, R4_p5, reset
  not not_3 (not_3_out, \end );
  // Register IR: pin names not known; wires that end beside it: bus_in, IR_p2, reset, out_29, IR_p5, 1'b1
  Counter #(.max('hffffffff), .width(32)) counter_1 (
    .count(1'b1), .Q(counter_1_q), .clk(IR_p2), .clr(reset));  // open: load, D, carry
  Counter #(.max('hffffffff), .width(32)) counter_2 (
    .count(1'b1), .Q(counter_2_q), .clk(and_5_out), .clr(reset));  // open: load, D, carry
  and and_5 (and_5_out, clkin, not_3_out);
  // Register IDX: pin names not known; wires that end beside it: out_13, bus_in, IDX_p3, bus_in, IDX_p5, reset
  // Probe on counter_1_q
  // Probe on counter_2_q
  Control control_1 (
    .r3_s(R2_p5), .r4_s(R3_p5), .idx_s(R4_p5), .fp_s(IDX_p5), .lr_s(control_1_lr_s),
    .on_scr_s(control_1_on_scr_s), .rstr_pc(program_counter_1_p8), .sp_id(control_1_sp_id), .ld_gr(ld_gr),
    .\end (\end ), .sv_pc(program_counter_1_p3), .ir_s(IR_p2), .mar_s(control_1_mar_s),
    .pc_s(program_counter_1_p2), .acc_s(ACC_p2), .mem_s(mem_s), .tmp_s(TMP_p2), .flags_s(FLAGS_p2),
    .sp_s(control_1_sp_s), .r0_s(R0_p2), .r1_s(R0_p8), .r2_s(R1_p5), .ints(control_1_ints), .asr(ASR),
    .lr_e(control_1_lr_e), .lr_id(alu_1_p15), .op0(alu_1_p5), .op1(alu_1_p4), .op2(alu_1_p3),
    .aux(maths_unit_1_p1[2]), .math_e(control_1_math_e[0]), .fpu_e(control_1_math_e[1]),
    .ack_int(control_1_ack_int), .plus1_e(set_to_one_1_p3), .pc_e(program_counter_1_p7), .mem_e(mem_e),
    .acc_e(ACC_p5), .sp_e(control_1_sp_e), .r0_e(R0_p6), .r1_e(R1_p3), .r2_e(R2_p3), .r3_e(R3_p3),
    .r4_e(R4_p3), .idx_e(IDX_p3), .fp_e(control_1_fp_e), .clks(clks), .clk(clk), .clke(clke), .reset(reset),
    .c(FLAGS_p5[5]), .a(FLAGS_p5[4]), .e(FLAGS_p5[3]), .z(FLAGS_p5[2]), .n(FLAGS_p5[1]), .\int (or_3_out),
    .halt(HALT), .v(FLAGS_p5[0]), .fcmp(FCMP), .ir(IR_p5));
  // Register FP: pin names not known; wires that end beside it: out_14, bus_in, control_1_fp_e, bus_in, control_1_lr_s, reset
  // Stack_Pointer stack_pointer_1: pin names not known; wires that end beside it: control_1_sp_s, control_1_sp_e, control_1_sp_id, reset, out_27, bus_in
  // Register LR: pin names not known; wires that end beside it: out_15, bus_in, control_1_lr_e
  // Register MAR: pin names not known; wires that end beside it: bus_in, control_1_mar_s, reset, mem_addr, 1'b1
  // Register register_1: pin names not known; wires that end beside it: ON_SCR_t, control_1_on_scr_s, reset, register_1_p4, 1'b1
  not not_4 (not_4_out, maths_unit_1_p1[2]);
  D_Flip_Flop d_ff_3 (.clk(CONT), .D(1'b1), .Q(d_ff_3_q), .reset(not_5_out));  // open: Qn, preset
  not not_5 (not_5_out, HALT);
  and and_6 (on_scr, ld_gr, or_4_out);
  or or_4 (or_4_out, register_1_p4, not_4_out);
  or or_5 (CL_EN, d_ff_3_q, not_5_out);

  assign bus_out = bus_in;
endmodule

module Graphics_Unit (
  input  bkgd,
  input  clk,
  input  en_ld,
  input  on_scr,
  input  set,
  input  [15:0] pos,
  input  [15:0] col,
  input  reset,
  output bg_rdy,
  output [7:0] X,
  output [7:0] Y,
  output [15:0] data,
  output scr_clk,
  output scr_en
);

  wire and_1_out, demultiplexer_1_out0, demultiplexer_1_out1, graphics_background_1_scr_clk,
       graphics_background_1_scr_en, graphics_foreground_1_scr_clk, graphics_foreground_1_scr_en;
  wire [7:0] graphics_background_1_x, graphics_background_1_y, graphics_foreground_1_x,
       graphics_foreground_1_y;
  wire [15:0] graphics_background_1_data, graphics_foreground_1_data;

  and and_1 (and_1_out, en_ld, on_scr);
  Demultiplexer #(.enable("false")) demultiplexer_1 (
    .out0(demultiplexer_1_out0), .out1(demultiplexer_1_out1), .in(clk), .sel(bg_rdy));
  Graphics_Background graphics_background_1 (
    .data(graphics_background_1_data), .Y(graphics_background_1_y), .X(graphics_background_1_x),
    .scr_en(graphics_background_1_scr_en), .scr_clk(graphics_background_1_scr_clk), .reset(reset),
    .bkgd(bkgd), .clk(demultiplexer_1_out0));
  Graphics_Foreground graphics_foreground_1 (
    .data(graphics_foreground_1_data), .Y(graphics_foreground_1_y), .X(graphics_foreground_1_x),
    .scr_en(graphics_foreground_1_scr_en), .scr_clk(graphics_foreground_1_scr_clk), .set(set), .pos(pos),
    .col(col), .reset(reset), .en_ld(and_1_out), .clk(demultiplexer_1_out1));
  not not_1 (bg_rdy, graphics_background_1_scr_en);
  Multiplexer #(.enable("false"), .width(8)) multiplexer_1 (
    .in0(graphics_background_1_x), .in1(graphics_foreground_1_x), .out(X), .sel(bg_rdy));
  Multiplexer #(.enable("false"), .width(8)) multiplexer_2 (
    .in0(graphics_background_1_y), .in1(graphics_foreground_1_y), .out(Y), .sel(bg_rdy));
  Multiplexer #(.enable("false"), .width(16)) multiplexer_3 (
    .in0(graphics_background_1_data), .in1(graphics_foreground_1_data), .out(data), .sel(bg_rdy));
  Multiplexer #(.enable("false")) multiplexer_4 (
    .in0(graphics_background_1_scr_clk), .in1(graphics_foreground_1_scr_clk), .out(scr_clk), .sel(bg_rdy));
  Multiplexer #(.enable("false")) multiplexer_5 (
    .in0(graphics_background_1_scr_en), .in1(graphics_foreground_1_scr_en), .out(scr_en), .sel(bg_rdy));
endmodule

module Control (
  input  clk,
  input  clke,
  input  reset,
  input  \int ,
  input  clks,
  input  c,
  input  a,
  input  e,
  input  z,
  input  n,
  input  v,
  input  [15:0] ir,
  output sv_pc,
  output ack_int,
  output plus1_e,
  output ir_s,
  output pc_e,
  output mar_s,
  output mem_e,
  output pc_s,
  output acc_e,
  output acc_s,
  output sp_e,
  output mem_s,
  output r0_e,
  output tmp_s,
  output r1_e,
  output flags_s,
  output r2_e,
  output sp_s,
  output r3_e,
  output r0_s,
  output r4_e,
  output r1_s,
  output idx_e,
  output r2_s,
  output fp_e,
  output r3_s,
  output lr_e,
  output r4_s,
  output idx_s,
  output lr_id,
  output op0,
  output fp_s,
  output op1,
  output lr_s,
  output op2,
  output on_scr_s,
  output aux,
  output rstr_pc,
  output math_e,
  output fpu_e,
  output sp_id,
  output ld_gr,
  output \end ,
  output halt,
  output ints,
  output asr,
  output fcmp
);

  wire _1WC, and_13_out, and_14_out, and_17_out, and_19_out, and_20_out, d_ff_2_q, jump_decoder_1_p11,
       nor_1_out, not_1_out, not_2_out, not_3_out, not_4_out, not_5_out, not_6_out, not_7_out, not_8_out,
       not_9_out, not_10_out, not_11_out, not_12_out, not_13_out, or_1_out, or_3_out, or_4_out, or_5_out,
       or_7_out, or_8_out, or_9_out, or_10_out, S5, S7;
  wire [2:0] counter_1_q, demux_3_8_1_p3, demux_3_8_2_p4_2;
  wire [4:0] demux_3_8_2_p4;
  wire [6:0] adder_1_out, rom_1_data;
  wire [7:0] bit_extender_1_out, demux_3_8_1_p4, demux_3_8_3_p4, demux_3_8_4_p4, demux_3_8_5_p4, REG_E, REG_S;
  wire [7:1] and_18_out;
  wire [29:0] multiplexer_1_out, rom_2_data;

  and and_1 (pc_e, clke, or_3_out);
  and and_2 (mem_e, clke, or_4_out);
  and and_3 (acc_e, clke, or_5_out);
  and and_4 (sp_e, clke, multiplexer_1_out[16]);
  and and_5 (r0_e, clke, REG_E[0]);
  and and_6 (r1_e, clke, REG_E[1]);
  and and_7 (r2_e, clke, REG_E[2]);
  and and_8 (r3_e, clke, REG_E[3]);
  and and_9 (r4_e, clke, REG_E[4]);
  and and_10 (idx_e, clke, REG_E[5]);
  and and_11 (fp_e, clke, REG_E[6]);
  and and_12 (lr_e, clke, REG_E[7]);
  // Jump_Decoder jump_decoder_1: pin names not known; wires that end beside it: c, a, e, z, n, v, ir[3], ir[2], ir[1], ir[0], jump_decoder_1_p11
  and and_13 (and_13_out, not_2_out, not_3_out, not_4_out, ir[12], ir[11]);
  and and_14 (and_14_out, not_5_out, ir[14], ir[13], not_6_out, not_7_out, S5);
  D_Flip_Flop d_ff_1 (.clk(and_14_out), .D(ir[0]), .Q(ints), .reset(reset));  // open: Qn, preset
  and and_15 (asr, ir[15], not_8_out, not_9_out, ir[12], ir[11], ir[0]);
  and and_16 (fcmp, ir[15], ir[14], not_10_out, ir[12], not_11_out, ir[0]);
  or or_1 (or_1_out, reset, and_17_out);
  and and_17 (and_17_out, multiplexer_1_out[29], nor_1_out, not_1_out);
  not not_1 (not_1_out, demux_3_8_2_p4[4]);
  or or_2 (plus1_e, ack_int, multiplexer_1_out[22]);
  or or_3 (or_3_out, ack_int, multiplexer_1_out[21]);
  or or_4 (or_4_out, demux_3_8_2_p4[2], multiplexer_1_out[20]);
  or or_5 (or_5_out, demux_3_8_2_p4[3], multiplexer_1_out[17]);
  ROM #(.addrWidth(5), .dataWidth(7)) rom_1 (.addr(ir[15:11]), .data(rom_1_data));
  ROM #(.addrWidth(7), .dataWidth(30)) rom_2 (.addr(adder_1_out), .data(rom_2_data));
  not not_2 (not_2_out, ir[15]);
  not not_3 (not_3_out, ir[14]);
  not not_4 (not_4_out, ir[13]);
  not not_5 (not_5_out, ir[15]);
  not not_6 (not_6_out, ir[12]);
  not not_7 (not_7_out, ir[11]);
  not not_8 (not_8_out, ir[14]);
  not not_9 (not_9_out, ir[13]);
  not not_10 (not_10_out, ir[13]);
  not not_11 (not_11_out, ir[11]);
  Counter #(.max('h5), .ongoal("stay"), .trigger("falling"), .width(3)) counter_1 (
    .count(1'b1), .Q(counter_1_q), .up(1'b1), .clk(clk), .clr(or_1_out));  // open: load, D, carry
  assign bit_extender_1_out = {{7{nor_1_out}}, nor_1_out};  // Bit_Extender bit_extender_1
  // Demux_3_8 demux_3_8_1: pin names not known; wires that end beside it: demux_3_8_1_p3[2], demux_3_8_1_p3[1], demux_3_8_1_p3[0], demux_3_8_1_p4
  Adder #(.width(7)) adder_1 (
    .a({4'b0000, demux_3_8_1_p3}), .b(rom_1_data), .out(adder_1_out), .cin(1'b0));  // open: cout
  // Demux_3_8 demux_3_8_2: pin names not known; wires that end beside it: counter_1_q[2], counter_1_q[1], counter_1_q[0], {demux_3_8_2_p4_2, demux_3_8_2_p4[4:2], ack_int, demux_3_8_2_p4[0]}
  assign {and_18_out[7:3], S7, and_18_out[1], S5} = bit_extender_1_out & demux_3_8_1_p4;  // AND_Gate and_18, 8 bits wide
  or or_6 (_1WC, ir[13], ir[14], ir[15]);
  Counter #(.max('h7), .trigger("falling"), .width(3)) counter_2 (
    .load(demux_3_8_2_p4[3]), .D(3'b000), .count(1'b1), .Q(demux_3_8_1_p3), .up(1'b1), .clk(clk), .clr(reset));  // open: carry
  nor nor_1 (nor_1_out, demux_3_8_2_p4[0], ack_int, demux_3_8_2_p4[2], demux_3_8_2_p4[3]);
  and and_19 (and_19_out, jump_decoder_1_p11, S7, and_13_out);
  Multiplexer #(.enable("false"), .width(30)) multiplexer_1 (
    .in0({30{1'b0}}), .in1(rom_2_data),
    .out({multiplexer_1_out[29], ld_gr, rstr_pc, multiplexer_1_out[26], fpu_e, math_e, aux, multiplexer_1_out[22:16], lr_id, op0, op1, op2, multiplexer_1_out[11:2], sp_id, multiplexer_1_out[0]}),
    .sel(nor_1_out));
  // Demux_3_8 demux_3_8_3: pin names not known; wires that end beside it: ir[10], ir[9], ir[8], demux_3_8_3_p4
  // Demux_3_8 demux_3_8_4: pin names not known; wires that end beside it: ir[7], ir[6], ir[5], demux_3_8_4_p4
  // Demux_3_8 demux_3_8_5: pin names not known; wires that end beside it: ir[4], ir[3], ir[2], demux_3_8_5_p4
  Multiplexer #(.enable("false"), .select(2), .width(8)) multiplexer_2 (
    .in0({8{1'b0}}), .in1(demux_3_8_3_p4), .in2(demux_3_8_4_p4), .in3(demux_3_8_5_p4), .out(REG_E),
    .sel(multiplexer_1_out[19:18]));
  Multiplexer #(.enable("false"), .select(2), .width(8)) multiplexer_3 (
    .in0({8{1'b0}}), .in1(demux_3_8_3_p4), .in2(demux_3_8_4_p4), .in3(demux_3_8_5_p4), .out(REG_S),
    .sel(multiplexer_1_out[5:4]));
  and and_20 (and_20_out, demux_3_8_2_p4[0], \int );
  not not_12 (not_12_out, d_ff_2_q);
  D_Flip_Flop d_ff_2 (.clk(\int ), .D(1'b1), .Q(d_ff_2_q), .reset(rstr_pc));  // open: Qn, preset
  or or_7 (or_7_out, demux_3_8_2_p4[2], multiplexer_1_out[11]);
  or or_8 (or_8_out, ack_int, multiplexer_1_out[10]);
  or or_9 (or_9_out, and_20_out, demux_3_8_2_p4[3], and_19_out, multiplexer_1_out[9]);
  or or_10 (or_10_out, ack_int, multiplexer_1_out[8]);
  not not_13 (not_13_out, aux);
  and and_21 (sv_pc, S5, not_12_out, _1WC, clks);
  and and_22 (ir_s, clks, or_7_out);
  and and_23 (mar_s, clks, or_8_out);
  and and_24 (pc_s, clks, or_9_out);
  and and_25 (acc_s, clks, or_10_out);
  and and_26 (mem_s, clks, multiplexer_1_out[7]);
  and and_27 (tmp_s, clks, multiplexer_1_out[6]);
  and and_28 (flags_s, clks, multiplexer_1_out[3]);
  and and_29 (sp_s, clks, multiplexer_1_out[2]);
  and and_30 (r0_s, clks, REG_S[0]);
  and and_31 (r1_s, clks, REG_S[1]);
  and and_32 (r2_s, clks, REG_S[2]);
  and and_33 (r3_s, clks, REG_S[3]);
  and and_34 (r4_s, clks, REG_S[4]);
  and and_35 (idx_s, clks, REG_S[5]);
  and and_36 (fp_s, clks, REG_S[6]);
  and and_37 (lr_s, clks, REG_S[7]);
  and and_38 (on_scr_s, clks, multiplexer_1_out[26]);
  and and_39 (\end , aux, multiplexer_1_out[0]);
  and and_40 (halt, not_13_out, multiplexer_1_out[0]);

  // Notes on the sheet:
  //   contents of rom_1 (hex, n*v repeats v):
  //   0 4 7 b f 12 17 1a 1f 21 23 26 2c 2d 2f 31 35 39 3d 41 45 48 4b 4e 52 56 5a 5d 5f 63 67 6a
  //   contents of rom_2 (hex, n*v repeats v):
  //   600500 100030 20200 20000000 200400 100200 20000000 600500 100200 20030 20000000 600500 20200 100000
  //   20000000 40400 100030 20000000 80040 40100 20400 100030 20000000 c0400 40080 20000000 80040 c0100
  //   20400 40080 20000000 40030 20000000 10030 20000000 40400 10080080 20000000 0 40040 7080100 20400
  //   108c0080 20000000 20000000 8000000 20000000 40200 20000000 4 10400 100030 20000000 10400 40080 6
  //   20000000 80040 40108 20030 20000000 80040 44108 20030 20000000 80040 4c108 20030 20000000 42108
  //   20010 20000000 4a108 20010 20000000 46108 20030 20000000 80040 41108 20030 20000000 80040 45108
  //   20030 20000000 80040 43108 20030 20000000 80040 47108 20000000 1 20000000 80040 1040108 20030
  //   20000000 80040 2040100 20030 20000000 2840100 20030 20000000 800001
  //   Fetch Counter
  //   uCode LUT
  //   uCode ROM
  //   Execute Counter
endmodule

module Graphics_Background (
  input  reset,
  input  bkgd,
  input  clk,
  output [15:0] data,
  output [7:0] Y,
  output [7:0] X,
  output scr_en,
  output scr_clk
);

  wire comparator_1_eq, comparator_2_eq, not_1_out;
  wire [15:0] bit_extender_1_out;
  wire [16:0] counter_1_q;

  and and_1 (scr_clk, bkgd, clk);
  Counter #(.max('h10000), .ongoal("stay"), .width(17)) counter_1 (
    .Q(counter_1_q), .clk(scr_clk), .clr(reset));  // open: load, D, count, carry
  Bit_Extender #(.in_width(17), .\type ("zero")) bit_extender_1 (.in(counter_1_q), .out(bit_extender_1_out));
  Counter counter_2 (.Q(X), .clk(scr_clk), .clr(reset));  // open: load, D, count, carry
  ROM #(.addrWidth(16), .dataWidth(16)) rom_1 (.addr(bit_extender_1_out), .data(data));
  Comparator #(.mode("unsigned")) comparator_1 (.a(X), .b({8{1'b0}}), .eq(comparator_1_eq));  // open: gt, lt
  Comparator #(.mode("unsigned"), .width(17)) comparator_2 (
    .a(counter_1_q), .b(17'h10000), .eq(comparator_2_eq));  // open: gt, lt
  Counter counter_3 (.Q(Y), .clk(comparator_1_eq), .clr(reset));  // open: load, D, count, carry
  not not_1 (not_1_out, comparator_2_eq);
  and and_2 (scr_en, not_1_out, bkgd);

  // Notes on the sheet:
  //   contents of rom_1 (hex, n*v repeats v):
  //   65536*ffd7
endmodule

module Graphics_Foreground (
  input  set,
  input  [15:0] pos,
  input  [15:0] col,
  input  reset,
  input  en_ld,
  input  clk,
  output [15:0] data,
  output [7:0] Y,
  output [7:0] X,
  output scr_en,
  output scr_clk
);

  wire [15:0] divider_1_out, divider_1_rem, register_1_q;

  and and_1 (scr_clk, en_ld, clk);
  Register #(.width(16)) register_1 (.D(pos), .Q(register_1_q), .clk(set), .clr(reset));  // open: en
  Divider #(.mode("unsigned"), .width(16)) divider_1 (
    .a(register_1_q), .b(16'h100), .out(divider_1_out), .rem(divider_1_rem));  // open: upper
  Register #(.width(16)) register_2 (.D(col), .Q(data), .clk(set), .clr(reset));  // open: en
  Bit_Extender #(.in_width(16), .out_width(8), .\type ("zero")) bit_extender_1 (.in(divider_1_out), .out(Y));
  Bit_Extender #(.in_width(16), .out_width(8), .\type ("zero")) bit_extender_2 (.in(divider_1_rem), .out(X));

  assign scr_en = en_ld;
endmodule

module KBD_Controller (
  input  [6:0] data,
  input  clk_e,
  input  en,
  input  [3:0] id,
  input  reset,
  input  [3:0] addr,
  output [15:0] bus_out,
  output kbd_clk
);

  wire and_1_out;
  wire [3:0] xnor_1_out;
  wire [15:0] bit_extender_1_out, register_1_q;

  assign xnor_1_out = ~(id ^ addr);  // XNOR_Gate xnor_1, 4 bits wide
  and and_1 (and_1_out, xnor_1_out[0], xnor_1_out[1], xnor_1_out[2], xnor_1_out[3]);
  and and_2 (kbd_clk, clk_e, en, and_1_out);
  assign bit_extender_1_out = {{9{1'b0}}, data};  // Bit_Extender bit_extender_1
  assign bus_out = kbd_clk ? register_1_q : 16'bz;  // Controlled_Buffer controlled_buffer_1
  Register #(.width(16)) register_1 (.D(bit_extender_1_out), .Q(register_1_q), .clk(kbd_clk), .clr(reset));  // open: en
endmodule

module TTY_Controller (
  input  [15:0] bus_in,
  input  clk_s,
  input  en,
  input  [3:0] id,
  input  [3:0] addr,
  output [6:0] data,
  output clk
);

  wire and_1_out;
  wire [3:0] xnor_1_out;

  Pull_Resistor pull_resistor_1 (.node(bus_in));
  assign xnor_1_out = ~(id ^ addr);  // XNOR_Gate xnor_1, 4 bits wide
  Bit_Extender #(.in_width(16), .out_width(7), .\type ("zero")) bit_extender_1 (.in(bus_in), .out(data));
  and and_1 (and_1_out, xnor_1_out[0], xnor_1_out[1], xnor_1_out[2], xnor_1_out[3]);
  and and_2 (clk, clk_s, en, and_1_out);
endmodule

module Input_Device (
  input  [15:0] data,
  input  clk_e,
  input  en,
  input  [3:0] id,
  input  [3:0] addr,
  input  reset,
  output [15:0] bus_out
);

  wire and_1_out, and_2_out;
  wire [3:0] xnor_1_out;

  assign xnor_1_out = ~(id ^ addr);  // XNOR_Gate xnor_1, 4 bits wide
  and and_1 (and_1_out, xnor_1_out[0], xnor_1_out[1], xnor_1_out[2], xnor_1_out[3]);
  and and_2 (and_2_out, clk_e, en, and_1_out);
  // Register register_1: pin names not known; wires that end beside it: data, 1'b1, reset, bus_out, and_2_out
endmodule

module Output_Device (
  input  [15:0] bus_in,
  input  clk_s,
  input  en,
  input  [3:0] id,
  input  reset,
  input  [3:0] addr,
  output [15:0] data
);

  wire and_1_out, and_2_out;
  wire [3:0] xnor_1_out;

  assign xnor_1_out = ~(id ^ addr);  // XNOR_Gate xnor_1, 4 bits wide
  and and_1 (and_1_out, clk_s, en, and_2_out);
  and and_2 (and_2_out, xnor_1_out[0], xnor_1_out[1], xnor_1_out[2], xnor_1_out[3]);
  // Register register_1: pin names not known; wires that end beside it: bus_in, and_1_out, reset, data, 1'b1
endmodule
